# Fritzing sketch garage_door_sensor (saved by Fritzing 0.8.7b)
circuit board: 8.46667cm x 5.64444cm

parts:
  2_Channel_Relay = 2 Channel Power Relay
  Sommer_Conex = Sommer Conex [package="Sommer Conex"]
  WeMos_D1_Mini = WeMos D1 Mini

nets:
  N1: 2_Channel_Relay.GND, WeMos_D1_Mini.G
  N2: 2_Channel_Relay.IN1, WeMos_D1_Mini.D5
  N3: 2_Channel_Relay.IN2, WeMos_D1_Mini.D6
  VCC: 2_Channel_Relay.VCC, WeMos_D1_Mini.5V
  N4: 2_Channel_Relay.K1-COM, 2_Channel_Relay.K2-COM, Sommer_Conex.SIG
  N5: 2_Channel_Relay.K1-NO, Sommer_Conex.T2
  N6: 2_Channel_Relay.K2-NO, Sommer_Conex.T1

custom parts:
  2 Channel Power Relay: A 2 channel power relay. The module operates at 5V.
  Sommer Conex: Female input for Sommer Conex module
  WeMos D1 Mini: The D1 mini is a mini wifi board based on ESP-8266EX.
